# Fritzing sketch Arduino_NRF24L01_Schematic (saved by Fritzing 0.9.3b)
circuit board: 8.46667cm x 5.64444cm
breadboards: 1

parts:
  Arduino_Uno = Arduino Uno (Rev3)
  NRF24L01+ = NRF24L01+ Breakout Board

nets:
  N1: Arduino_Uno.D11_PWM/MOSI, NRF24L01+.MOSI
  N2: Arduino_Uno.D12/MISO, NRF24L01+.MISO
  N3: Arduino_Uno.D13/SCK, NRF24L01+.SCK
  3V3: Arduino_Uno.3V3, NRF24L01+.VCC
  GND: Arduino_Uno.GND, NRF24L01+.GND
