# Fritzing sketch RPI_NRF24L01_Schematic (saved by Fritzing 0.9.3b)
breadboards: 1

parts:
  Raspberry_Pi_1 = Raspberry Pi 4 [part_number=RPI-4-b]
  NRF24L01+ = NRF24L01+ Breakout Board

nets:
  3V3: Raspberry_Pi_1.3v3, Raspberry_Pi_1.3V3, NRF24L01+.VCC
  N1: Raspberry_Pi_1.GPIO17, NRF24L01+.CS
  N2: Raspberry_Pi_1.GPIO10, NRF24L01+.MOSI
  N3: Raspberry_Pi_1.GPIO9, NRF24L01+.MISO
  N4: Raspberry_Pi_1.GPIO11, NRF24L01+.SCK
  GND: Raspberry_Pi_1.GND, NRF24L01+.GND

custom parts:
  Raspberry Pi 4: The RPi4, a faster version of the awesome Raspberry Pi 2 B ARM Board with 40 pin gpio. Ready for special Raspberry Pi B+ and RPi2 Hat (Hardware attached (on) top)
